# Fritzing sketch spectre_remote (saved by Fritzing 0.9.4)
breadboards: 1

parts:
  U2 = V_REG_LD1117VXX [package=78xxl]
  U3 = LIPO-600mAh [package=lipo-600]
  U4 = ESP32-38PinWide [part_number=ESP32-38PinWide]
  R1 = Resistor [tolerance=±5% resistance=36 package="0805 [SMD]"]
  R2 = Resistor [tolerance=±5% resistance=220 package="0805 [SMD]"]
  Q1 = npn-Powertransistor [package="TO220 [THT]"]
  U5 = Vibration Motor- ROB-08449 [package=vibe-motor-10mm]

nets:
  N1: U2.OUT, U4.3.3, R1.Pin_1
  GND: U2.GND, U3.-, U4.GND, Q1.emitter
  N2: U2.IN, U3.+
  N3: U4.GPIO13, R2.Pin_1
  N4: R1.Pin_0, U5.-
  N5: R2.Pin_0, Q1.base
  N6: Q1.collector, U5.+

custom parts:
  V_REG_LD1117VXX: LD1117VXX voltage regulator. We carry the 3.3V version (COM-00526) in TO-220 package.
  LIPO-600mAh: 600mAh Lipo-battery
  ESP32-38PinWide: Generic 38-Pin ESP32 with wide format (only access to one side of pins on a breadboard) based on Stephen Lilley's HiLetgo ESP-WROOM-32 ESP32 ESP-32S Development Board.
